// Logisim project address_decode.circ as structural Verilog: 1 circuit, main circuit main
module main (
);

  wire A0, A1, A2, A3, A4, A5, A6, A7, A8, A9, A10, A11, A12, A13, A13OR12, A14, A15, and_3_out, and_4_out,
       and_5_out, and_6_out, and_7_out, and_8_out, and_9_out, and_10_out, and_11_out, and_12_out, and_13_out,
       and_14_out, and_15_out, and_16_out, and_17_out, and_18_out, and_19_out, B1, B2, BANK, BB, BSS, C006,
       C007, C030, CLK, CXXX, decoder_1_out0, decoder_1_out3, decoder_1_out5, decoder_1_out8, decoder_2_out0,
       decoder_2_out1, decoder_2_out2, decoder_2_out3, decoder_2_out4, decoder_2_out5, decoder_2_out6,
       decoder_2_out7, decoder_2_out8, decoder_2_out9, decoder_2_out10, decoder_2_out11, decoder_2_out12,
       decoder_2_out13, decoder_2_out14, decoder_2_out15, DEV, DXXX, FF, FULLMODE, GFXMODE, GFXSS, HIRES,
       KBD, LORES, LOW0, MIXMODE, nand_1_out, nand_2_out, nand_3_out, nand_4_out, nand_7_out, nand_8_out,
       nand_9_out, nand_10_out, nand_11_out, nand_12_out, nand_18_out, not_1_out, not_2_out, not_3_out,
       not_4_out, not_5_out, not_6_out, not_11_out, not_12_out, not_13_out, NOWRITE, or_4_out, or_6_out,
       or_7_out, or_9_out, or_10_out, or_11_out, or_13_out, or_14_out, or_15_out, or_17_out, or_20_out,
       or_21_out, or_23_out, or_24_out, or_25_out, or_26_out, or_27_out, or_28_out, or_30_out, or_31_out,
       or_32_out, or_33_out, or_34_out, or_35_out, or_36_out, or_37_out, or_38_out, PAGE1, PAGE2, RAMWRITE,
       READROM, RW, SS, TXTMODE, x0, x00, x000, x1, x2, x3, x4, x5, x6, x7, x8, x9, x30, x50, x80, xA, xB;

  or or_1 (SS, CXXX, x000);
  and and_1 (B1, BANK, nand_2_out);
  nand nand_1 (nand_1_out, not_3_out, A3);
  not not_1 (not_1_out, A13);
  not not_2 (not_2_out, A12);
  nand nand_2 (nand_2_out, nand_1_out, nand_3_out);
  not not_3 (not_3_out, BSS);
  or or_2 (GFXSS, SS, x50);
  and and_2 (B2, BANK, nand_3_out);
  nand nand_3 (nand_3_out, nand_2_out, nand_4_out);
  nand nand_4 (nand_4_out, not_4_out, not_3_out);
  not not_4 (not_4_out, A3);
  Hex_Digit_Display hex_digit_display_1 (.value({A15, A14, A13, A12}));  // open: dp
  DipSwitch #(.number(16)) dipswitch_1 (
    .sw1(A15), .sw2(A14), .sw3(A13), .sw4(A12), .sw5(A11), .sw6(A10), .sw7(A9), .sw8(A8), .sw9(A7),
    .sw10(A6), .sw11(A5), .sw12(A4), .sw13(A3), .sw14(A2), .sw15(A1), .sw16(A0));
  and and_3 (and_3_out, A15, A14);
  nand nand_5 (CXXX, and_3_out, and_4_out);
  and and_4 (and_4_out, not_2_out, not_1_out);
  nand nand_6 (DXXX, not_1_out, A12);
  or or_3 (BSS, SS, x80);
  Clock clock_1 (.out(CLK));
  Hex_Digit_Display hex_digit_display_2 (.value({A11, A10, A9, A8}));  // open: dp
  Hex_Digit_Display hex_digit_display_3 (.value({A7, A6, A5, A4}));  // open: dp
  or or_4 (or_4_out, BSS, xA);
  Hex_Digit_Display hex_digit_display_4 (.value({A3, A2, A1, A0}));  // open: dp
  or or_5 (LOW0, x00, x0);
  nand nand_7 (nand_7_out, and_5_out, and_7_out);
  and and_5 (and_5_out, or_4_out, or_6_out);
  or or_6 (or_6_out, BSS, x2);
  or or_7 (or_7_out, BSS, x9);
  or or_8 (C007, x7, or_13_out);
  or or_9 (or_9_out, nand_8_out, nand_9_out);
  nand nand_8 (nand_8_out, and_5_out, and_6_out);
  and and_6 (and_6_out, or_7_out, or_15_out);
  DipSwitch #(.number(5)) dipswitch_2 (.sw5(RW));  // open: sw1, sw2, sw3, sw4
  or or_10 (or_10_out, A11, A10);
  or or_11 (or_11_out, A9, A8);
  or or_12 (C006, or_13_out, x6);
  or or_13 (or_13_out, SS, x00);
  or or_14 (or_14_out, BSS, x0);
  or or_15 (or_15_out, BSS, x1);
  LED u_dev (.in(DEV));
  or or_16 (DEV, not_5_out, or_17_out);
  not not_5 (not_5_out, KBD);
  or or_17 (or_17_out, nand_11_out, or_21_out);
  or or_18 (A13OR12, A13, A12);
  or or_19 (x000, or_10_out, or_11_out);
  J_K_Flip_Flop j_k_ff_1 (
    .J(FF), .K(NOWRITE), .clk(or_9_out), .Q(RAMWRITE), .Qn(NOWRITE), .reset(nand_7_out));  // open: preset
  nand nand_9 (nand_9_out, and_7_out, and_10_out);
  and and_7 (and_7_out, or_14_out, or_20_out);
  or or_20 (or_20_out, BSS, x8);
  or or_21 (or_21_out, A13OR12, A11);
  or or_22 (C030, x0, or_23_out);
  or or_23 (or_23_out, SS, x30);
  J_K_Flip_Flop j_k_ff_2 (.J(nand_8_out), .K(nand_9_out), .clk(CLK), .Q(READROM), .Qn(BANK));  // open: preset, reset
  LED ram (.in(nand_10_out));
  nand nand_10 (nand_10_out, DEV, and_8_out);
  nand nand_11 (nand_11_out, A14, A15);
  or or_24 (or_24_out, and_6_out, and_10_out);
  or or_25 (or_25_out, BSS, x3);
  LED rom (.in(and_8_out));
  and and_8 (and_8_out, or_26_out, nand_12_out);
  or or_26 (or_26_out, or_27_out, or_30_out);
  or or_27 (or_27_out, nand_11_out, and_9_out);
  and and_9 (and_9_out, not_6_out, not_12_out);
  not not_6 (not_6_out, A12);
  Decoder #(.select(4)) decoder_1 (
    .out0(decoder_1_out0), .out3(decoder_1_out3), .out5(decoder_1_out5), .out8(decoder_1_out8),
    .sel({A7, A6, A5, A4}));  // open: out1, out2, out4, out6, out7, out9, out10, out11, out12, out13, out14, out15, en
  not not_7 (x00, decoder_1_out0);
  J_K_Flip_Flop j_k_ff_3 (.J(or_24_out), .K(1'b0), .clk(CLK), .Q(FF), .reset(nand_7_out));  // open: Qn, preset
  and and_10 (and_10_out, or_25_out, or_28_out);
  or or_28 (or_28_out, BSS, xB);
  nand nand_12 (nand_12_out, and_11_out, not_11_out);
  and and_11 (and_11_out, and_12_out, BB);
  and and_12 (and_12_out, A13OR12, A15);
  not not_8 (x30, decoder_1_out3);
  not not_9 (x50, decoder_1_out5);
  not not_10 (x80, decoder_1_out8);
  LED u_KBD (.in(KBD));
  or or_29 (KBD, SS, LOW0);
  not not_11 (not_11_out, A14);
  or or_30 (or_30_out, and_13_out, and_16_out);
  and and_13 (and_13_out, BANK, RW);
  not not_12 (not_12_out, A13);
  LED A16 (.in(and_14_out));
  and and_14 (and_14_out, and_15_out, and_17_out);
  and and_15 (and_15_out, or_30_out, B2);
  and and_16 (and_16_out, RAMWRITE, not_13_out);
  LED GFX (.in(or_31_out));
  or or_31 (or_31_out, GFXSS, x0);
  nand nand_13 (PAGE1, or_32_out, PAGE2);
  LED u_PAGE1 (.in(or_32_out));
  or or_32 (or_32_out, GFXSS, x4);
  and and_17 (and_17_out, A12, and_18_out);
  not not_13 (not_13_out, RW);
  nand nand_14 (GFXMODE, or_31_out, TXTMODE);
  nand nand_15 (BB, C007, nand_18_out);
  and and_18 (and_18_out, not_12_out, and_19_out);
  and and_19 (and_19_out, A14, A15);
  Decoder #(.select(4)) decoder_2 (
    .out0(decoder_2_out0), .out1(decoder_2_out1), .out2(decoder_2_out2), .out3(decoder_2_out3),
    .out4(decoder_2_out4), .out5(decoder_2_out5), .out6(decoder_2_out6), .out7(decoder_2_out7),
    .out8(decoder_2_out8), .out9(decoder_2_out9), .out10(decoder_2_out10), .out11(decoder_2_out11),
    .out12(decoder_2_out12), .out13(decoder_2_out13), .out14(decoder_2_out14), .out15(decoder_2_out15),
    .sel({A3, A2, A1, A0}));  // open: en
  not not_14 (x0, decoder_2_out0);
  not not_15 (x1, decoder_2_out1);
  not not_16 (x2, decoder_2_out2);
  not not_17 (x3, decoder_2_out3);
  not not_18 (x4, decoder_2_out4);
  nand nand_16 (TXTMODE, GFXMODE, or_33_out);
  LED TXT (.in(or_33_out));
  or or_33 (or_33_out, GFXSS, x1);
  nand nand_17 (PAGE2, PAGE1, or_34_out);
  LED u_PAGE2 (.in(or_34_out));
  or or_34 (or_34_out, GFXSS, x5);
  nand nand_18 (nand_18_out, BB, C006);
  not not_19 (x5, decoder_2_out5);
  not not_20 (x6, decoder_2_out6);
  not not_21 (x7, decoder_2_out7);
  not not_22 (x8, decoder_2_out8);
  not not_23 (x9, decoder_2_out9);
  not not_24 (xA, decoder_2_out10);
  not not_25 (xB, decoder_2_out11);
  // NOT_Gate not_26 has open pins: in=decoder_2_out12, out=open
  // NOT_Gate not_27 has open pins: in=decoder_2_out13, out=open
  // NOT_Gate not_28 has open pins: in=decoder_2_out14, out=open
  // NOT_Gate not_29 has open pins: in=decoder_2_out15, out=open
  LED FULL (.in(or_35_out));
  or or_35 (or_35_out, GFXSS, x2);
  LED u_LORES (.in(or_36_out));
  or or_36 (or_36_out, GFXSS, x6);
  nand nand_19 (FULLMODE, or_35_out, MIXMODE);
  LED MIX (.in(or_37_out));
  or or_37 (or_37_out, GFXSS, x3);
  nand nand_20 (LORES, or_36_out, HIRES);
  nand nand_21 (HIRES, LORES, or_38_out);
  nand nand_22 (MIXMODE, FULLMODE, or_37_out);
  LED u_HIRES (.in(or_38_out));
  or or_38 (or_38_out, GFXSS, x7);
endmodule
